// Logisim project task1.circ as structural Verilog: 1 circuit, main circuit main
module main (
  input  in_1,
  input  in_2,
  input  in_3,
  input  in_4,
  input  in_5,
  input  in_6,
  input  in_7,
  input  in_8,
  input  in_9,
  input  in_10,
  input  in_11,
  input  in_12,
  input  in_13,
  output out_14,
  output out_15,
  output out_16,
  output out_17,
  output out_18,
  output out_19,
  output out_20,
  output out_21
);

  not not_1 (out_14, in_3);
  nand nand_1 (out_17, in_6, in_9);
  and and_1 (out_15, in_1, in_4);
  nor nor_1 (out_18, in_7, in_10);
  xor xor_1 (out_20, in_12, in_13);
  and and_2 (out_21, in_12, in_13);
  or or_1 (out_16, in_2, in_5);
  xor xor_2 (out_19, in_8, in_11);

  // Notes on the sheet:
  //   NOT GATE
  //   NAND GATE
  //   AND GATE
  //   NOR GATE
  //   HALF ADDER CIRCUIT
  //   OR GATE
  //   XOR GATE
endmodule
